// Logisim project alpha.circ as structural Verilog: 14 circuits, main circuit alpha_core
module alpha_core (
  input  [31:0] mem_in,
  input  clk,
  input  rst,
  output [31:0] mem_addr,
  output [31:0] mem_out,
  output mem_write,
  output [1:0] state
);

  wire control_unit_1_illegal, or_1_out, or_2_out, state_machine_1_load_inst, state_machine_1_mem_rd,
       state_machine_1_mem_w, subword_processing_1_illegal_out;
  wire [1:0] state_machine_1_mem_select, state_machine_1_pc_select, state_machine_1_rd_select;
  wire [2:0] instruction_decode_1_funct3;
  wire [3:0] instruction_type_1_inst_t;
  wire [4:0] instruction_decode_1_rd, instruction_decode_1_rs1, instruction_decode_1_rs2;
  wire [6:0] instruction_decode_1_funct7, instruction_decode_1_opcode;
  wire [31:0] control_unit_1_rd_val, instruction_decode_1_imm_b, instruction_decode_1_imm_i,
       instruction_decode_1_imm_j, instruction_decode_1_imm_s, instruction_decode_1_imm_u, multiplexer_1_out,
       multiplexer_2_out, program_counter_1_pc, program_counter_1_pc_next, register_1_q,
       register_file_1_rs1_out, register_file_1_rs2_out, subword_processing_1_rd_out;

  Register #(.width(32)) register_1 (
    .D(mem_in), .en(state_machine_1_load_inst), .clk(clk), .Q(register_1_q), .clr(rst));
  instruction_decode instruction_decode_1 (
    .instruction(register_1_q), .opcode(instruction_decode_1_opcode), .rd(instruction_decode_1_rd),
    .funct3(instruction_decode_1_funct3), .rs1(instruction_decode_1_rs1), .rs2(instruction_decode_1_rs2),
    .funct7(instruction_decode_1_funct7), .imm_i(instruction_decode_1_imm_i),
    .imm_s(instruction_decode_1_imm_s), .imm_b(instruction_decode_1_imm_b),
    .imm_u(instruction_decode_1_imm_u), .imm_j(instruction_decode_1_imm_j));
  instruction_type instruction_type_1 (.opcode(instruction_decode_1_opcode), .inst_t(instruction_type_1_inst_t));
  state_machine state_machine_1 (
    .inst_t(instruction_type_1_inst_t), .illegal(or_2_out), .clk(clk), .rst(rst),
    .rd_select(state_machine_1_rd_select), .pc_select(state_machine_1_pc_select),
    .mem_select(state_machine_1_mem_select), .mem_w(state_machine_1_mem_w), .mem_rd(state_machine_1_mem_rd),
    .load_inst(state_machine_1_load_inst), .state(state));
  or or_1 (or_1_out, state_machine_1_rd_select[0], state_machine_1_rd_select[1]);
  Multiplexer #(.select(2), .width(32)) multiplexer_1 (
    .in0(program_counter_1_pc), .in1(program_counter_1_pc_next), .in2(control_unit_1_rd_val),
    .in3(subword_processing_1_rd_out), .out(multiplexer_1_out), .sel(state_machine_1_rd_select));
  Multiplexer #(.select(2), .width(32)) multiplexer_2 (
    .in0(program_counter_1_pc), .in1(program_counter_1_pc_next), .in2(control_unit_1_rd_val),
    .in3(subword_processing_1_rd_out), .out(multiplexer_2_out), .sel(state_machine_1_pc_select));
  and and_1 (mem_write, state_machine_1_mem_w, ~or_2_out);  // AND_Gate
  register_file register_file_1 (
    .rs1(instruction_decode_1_rs1), .rs2(instruction_decode_1_rs2), .rd(instruction_decode_1_rd),
    .rd_in(multiplexer_1_out), .rd_w(or_1_out), .clk(clk), .rst(rst), .rs1_out(register_file_1_rs1_out),
    .rs2_out(register_file_1_rs2_out));
  program_counter program_counter_1 (
    .pc_in(multiplexer_2_out), .clk(clk), .rst(rst), .pc(program_counter_1_pc),
    .pc_next(program_counter_1_pc_next));
  subword_processing subword_processing_1 (
    .mem_addr(control_unit_1_rd_val), .mem_in(mem_in), .rs2_val(register_file_1_rs2_out),
    .funct3(instruction_decode_1_funct3), .mem_rd_in(state_machine_1_mem_rd),
    .mem_w_in(state_machine_1_mem_w), .mem_out(mem_out), .rd_out(subword_processing_1_rd_out),
    .illegal_out(subword_processing_1_illegal_out));
  Multiplexer #(.select(2), .width(32)) multiplexer_3 (
    .in0(program_counter_1_pc), .in1(program_counter_1_pc_next), .in2(control_unit_1_rd_val),
    .in3(program_counter_1_pc), .out(mem_addr), .sel(state_machine_1_mem_select));
  control_unit control_unit_1 (
    .rs1(register_file_1_rs1_out), .rs2(register_file_1_rs2_out), .pc(program_counter_1_pc),
    .pc_next(program_counter_1_pc_next), .imm_i(instruction_decode_1_imm_i),
    .imm_s(instruction_decode_1_imm_s), .imm_b(instruction_decode_1_imm_b),
    .imm_u(instruction_decode_1_imm_u), .imm_j(instruction_decode_1_imm_j),
    .inst_t(instruction_type_1_inst_t), .funct3(instruction_decode_1_funct3),
    .funct7(instruction_decode_1_funct7), .rd_val(control_unit_1_rd_val), .illegal(control_unit_1_illegal));
  or or_2 (or_2_out, subword_processing_1_illegal_out, control_unit_1_illegal);

  // Notes on the sheet:
  //   alpha - a simple RV32I core
  //   The core expects RAM, ROM and any peripherals to be connected to the same memory bus. Execution starts at address 0.
  //   The 'rst' pin is asynchronous. It zeroes out all registers and resets the state machine to initial state.
endmodule

module instruction_type (
  input  [6:0] opcode,
  output [3:0] inst_t
);

  PLA #(.in_width(7), .out_width(4), .\table ("xxxxxx0 0000 # X (compressed)\nxxxxx01 0000 # X (compressed)\n0000011 0101 # LOAD\n0000111 0000 # X (LOAD-FP)\n0001011 0000 # X (custom-0)\n0001111 0000 # X (MISC-MEM)\n0010011 0010 # OP-IMM\n0010111 0011 # AUIPC\n0011011 0000 # X (OP-IMM-32)\n0011111 0000 # X (48b inst)\n0100011 0110 # STORE\n0100111 0000 # X (STORE-FP)\n0101011 0000 # X (custom-1)\n0101111 0000 # X (AMO)\n0110011 0001 # OP\n0110111 0100 # LUI\n0111011 0000 # X (OP-32)\n0111111 0000 # X (64b inst)\n1000011 0000 # X (MADD)\n1000111 0000 # X (MSUB)\n1001011 0000 # X (NMSUB)\n1001111 0000 # X (NMADD)\n1010011 0000 # X (OP-FP)\n1010111 0000 # X (reserved)\n1011011 0000 # X (custom-2)\n1011111 0000 # X (48b inst)\n1100011 0111 # BRANCH\n1100111 1000 # JALR\n1101011 0000 # X (reserved)\n1101111 1001 # JAL\n1110011 1010 # SYSTEM\n1110111 0000 # X (reserved)\n1111011 0000 # X (custom-3)\n1111111 0000 # X (80b+ inst)")) pla_1 (
    .in(opcode), .out(inst_t));

  // Notes on the sheet:
  //   Instruction type decode
  //   Decodes the instruction type from the opcode. Values for inst_t are documented in the alpha.md file.
endmodule

module instruction_decode (
  input  [31:0] instruction,
  output [6:0] opcode,
  output [4:0] rd,
  output [2:0] funct3,
  output [4:0] rs1,
  output [4:0] rs2,
  output [6:0] funct7,
  output [31:0] imm_i,
  output [31:0] imm_s,
  output [31:0] imm_b,
  output [31:0] imm_u,
  output [31:0] imm_j
);

  assign imm_i = {{20{instruction[31]}}, instruction[31:20]};  // Bit_Extender bit_extender_1
  assign imm_s = {{20{instruction[31]}}, {instruction[31:25], instruction[11:7]}};  // Bit_Extender bit_extender_2
  assign imm_b = {{19{instruction[31]}}, {instruction[31], instruction[7], instruction[30:25], instruction[11:8], 1'b0}};  // Bit_Extender bit_extender_3
  assign imm_j = {{11{instruction[31]}}, {instruction[31], instruction[19:12], instruction[20], instruction[30:21], 1'b0}};  // Bit_Extender bit_extender_4

  assign funct3 = instruction[14:12];
  assign funct7 = instruction[31:25];
  assign imm_u = {instruction[31:12], {12{1'b0}}};
  assign opcode = instruction[6:0];
  assign rd = instruction[11:7];
  assign rs1 = instruction[19:15];
  assign rs2 = instruction[24:20];

  // Notes on the sheet:
  //   Instruction decode
  //   Decodes a 32-bit instruction into parts for all instruction types.
endmodule

module state_machine (
  input  [3:0] inst_t,
  input  illegal,
  input  clk,
  input  rst,
  output [1:0] rd_select,
  output [1:0] pc_select,
  output [1:0] mem_select,
  output mem_w,
  output mem_rd,
  output load_inst,
  output [1:0] state
);

  wire [1:0] pla_6_out;
  wire [3:0] multiplexer_1_out;
  wire [4:4] pla_1_out;

  Multiplexer #(.width(4)) multiplexer_1 (.in0(inst_t), .in1(4'b0000), .out(multiplexer_1_out), .sel(illegal));
  PLA #(.out_width(1), .\table ("00 1 # continue\n01 0 # single\n10 1 # double\n11 0 # halt")) pla_1 (
    .in(state), .out(pla_1_out[4]));
  PLA #(.in_width(5), .\table ("00000 00 # X\n00001 10 # OP\n00010 10 # OP_IMM\n00011 10 # AUIPC\n00100 10 # LUI\n00101 11 # LOAD\n00110 00 # STORE\n00111 00 # BRANCH\n01000 01 # JALR\n01001 01 # JAL\n01010 00 # SYSTEM\n01011 00 # X\n011xx 00 # X\n1xxxx 00 # continue")) pla_2 (
    .in({pla_1_out[4], multiplexer_1_out}), .out(rd_select));
  PLA #(.in_width(5), .\table ("00000 00 # X\n00001 01 # OP\n00010 01 # OP_IMM\n00011 01 # AUIPC\n00100 01 # LUI\n00101 01 # LOAD\n00110 01 # STORE\n00111 10 # BRANCH\n01000 10 # JALR\n01001 10 # JAL\n01010 00 # SYSTEM\n01011 00 # X\n011xx 00 # X\n1xxxx 00 # continue")) pla_3 (
    .in({pla_1_out[4], multiplexer_1_out}), .out(pc_select));
  PLA #(.in_width(5), .out_width(4), .\table ("00000 0000 # X\n00001 0001 # OP\n00010 0001 # OP_IMM\n00011 0001 # AUIPC\n00100 0001 # LUI\n00101 1010 # LOAD\n00110 0110 # STORE\n00111 0000 # BRANCH\n01000 0000 # JALR\n01001 0000 # JAL\n01010 0000 # SYSTEM\n01011 0000 # X\n011xx 0000 # X\n1xxxx 0000 # continue")) pla_4 (
    .in({pla_1_out[4], multiplexer_1_out}), .out({mem_rd, mem_w, mem_select}));
  PLA #(.in_width(5), .out_width(1), .\table ("00000 0 # X\n00001 1 # OP\n00010 1 # OP_IMM\n00011 1 # AUIPC\n00100 1 # LUI\n00101 0 # LOAD\n00110 0 # STORE\n00111 0 # BRANCH\n01000 0 # JALR\n01001 0 # JAL\n01010 0 # SYSTEM\n01011 0 # X\n011xx 0 # X\n1xxxx 1 # continue")) pla_5 (
    .in({pla_1_out[4], multiplexer_1_out}), .out(load_inst));
  PLA #(.in_width(5), .\table ("00000 11 # X\n00001 01 # OP\n00010 01 # OP_IMM\n00011 01 # AUIPC\n00100 01 # LUI\n00101 10 # LOAD\n00110 10 # STORE\n00111 00 # BRANCH\n01000 00 # JALR\n01001 00 # JAL\n01010 11 # SYSTEM\n01011 11 # X\n011xx 11 # X\n1xxxx 01 # continue")) pla_6 (
    .in({pla_1_out[4], multiplexer_1_out}), .out(pla_6_out));
  Register #(.width(2)) register_1 (.D(pla_6_out), .en(1'b1), .clk(clk), .Q(state), .clr(rst));

  // Notes on the sheet:
  //   State machine
  //   Generates the intermediate states of the core. States are described in the alpha.md file.
  //   0 => none, 1 => pc_next, 2 => rd_val, 3 => mem
  //   0 => pc, 1 => pc_next, 2 => rd_val
  //   0 => pc, 1 => pc_next, 2 => rd_val
endmodule

module subword_processing (
  input  [31:0] mem_addr,
  input  [31:0] mem_in,
  input  [31:0] rs2_val,
  input  [2:0] funct3,
  input  mem_rd_in,
  input  mem_w_in,
  output [31:0] mem_out,
  output [31:0] rd_out,
  output illegal_out
);

  wire and_1_out, and_2_out, subword_load_processing_1_illegal_out, subword_store_processing_1_illegal_out;

  subword_load_processing subword_load_processing_1 (
    .mem_addr(mem_addr), .mem_in(mem_in), .funct3(funct3),
    .illegal_out(subword_load_processing_1_illegal_out), .rd_out(rd_out));
  subword_store_processing subword_store_processing_1 (
    .mem_addr(mem_addr), .mem_in(mem_in), .rs2_val(rs2_val), .funct3(funct3),
    .illegal_out(subword_store_processing_1_illegal_out), .mem_out(mem_out));
  and and_1 (and_1_out, subword_load_processing_1_illegal_out, mem_rd_in);
  and and_2 (and_2_out, subword_store_processing_1_illegal_out, mem_w_in);
  or or_1 (illegal_out, and_1_out, and_2_out);

  // Notes on the sheet:
  //   Subword processing
  //   Extracts and inserts smaller units of data into a machine word. Split into load processing and store processing.
endmodule

module subword_load_processing (
  input  [31:0] mem_addr,
  input  [31:0] mem_in,
  input  [2:0] funct3,
  output illegal_out,
  output [31:0] rd_out
);

  wire or_1_out;
  wire [7:0] multiplexer_2_out;
  wire [15:0] multiplexer_1_out;
  wire [31:0] bit_extender_1_out, bit_extender_2_out, bit_extender_3_out, bit_extender_4_out,
       multiplexer_4_out, multiplexer_5_out;

  Multiplexer #(.width(16)) multiplexer_1 (
    .in0(mem_in[15:0]), .in1(mem_in[31:16]), .out(multiplexer_1_out), .sel(mem_addr[1]));
  Multiplexer #(.select(2), .width(8)) multiplexer_2 (
    .in0(mem_in[7:0]), .in1(mem_in[15:8]), .in2(mem_in[23:16]), .in3(mem_in[31:24]), .out(multiplexer_2_out),
    .sel(mem_addr[1:0]));
  or or_1 (or_1_out, mem_addr[1], funct3[2], mem_addr[0]);
  assign bit_extender_1_out = {{16{multiplexer_1_out[15]}}, multiplexer_1_out};  // Bit_Extender bit_extender_1
  assign bit_extender_2_out = {{16{1'b0}}, multiplexer_1_out};  // Bit_Extender bit_extender_2
  assign bit_extender_3_out = {{24{multiplexer_2_out[7]}}, multiplexer_2_out};  // Bit_Extender bit_extender_3
  assign bit_extender_4_out = {{24{1'b0}}, multiplexer_2_out};  // Bit_Extender bit_extender_4
  Multiplexer #(.select(2)) multiplexer_3 (
    .in0(1'b0), .in1(mem_addr[0]), .in2(or_1_out), .in3(1'b1), .out(illegal_out), .sel(funct3[1:0]));
  Multiplexer #(.width(32)) multiplexer_4 (
    .in0(bit_extender_1_out), .in1(bit_extender_2_out), .out(multiplexer_4_out), .sel(funct3[2]));
  Multiplexer #(.width(32)) multiplexer_5 (
    .in0(bit_extender_3_out), .in1(bit_extender_4_out), .out(multiplexer_5_out), .sel(funct3[2]));
  Multiplexer #(.select(2), .width(32)) multiplexer_6 (
    .in0(multiplexer_5_out), .in1(multiplexer_4_out), .in2(mem_in), .in3(mem_in), .out(rd_out),
    .sel(funct3[1:0]));

  // Notes on the sheet:
  //   Subword load processing
  //   Extracts and properly extends a data unit from a memory word to store in a register.
endmodule

module subword_store_processing (
  input  [31:0] mem_addr,
  input  [31:0] mem_in,
  input  [31:0] rs2_val,
  input  [2:0] funct3,
  output illegal_out,
  output [31:0] mem_out
);

  wire multiplexer_11_out, or_1_out;
  wire [7:0] multiplexer_3_out, multiplexer_4_out, multiplexer_5_out, multiplexer_6_out, multiplexer_7_out,
       multiplexer_8_out, multiplexer_9_out, multiplexer_10_out;
  wire [15:0] multiplexer_1_out, multiplexer_2_out;

  or or_1 (or_1_out, mem_addr[0], mem_addr[1]);
  Multiplexer #(.width(16)) multiplexer_1 (
    .in0(rs2_val[15:0]), .in1(mem_in[15:0]), .out(multiplexer_1_out), .sel(mem_addr[1]));
  Multiplexer #(.width(16)) multiplexer_2 (
    .in0(mem_in[31:16]), .in1(rs2_val[15:0]), .out(multiplexer_2_out), .sel(mem_addr[1]));
  Multiplexer #(.width(8)) multiplexer_3 (
    .in0(rs2_val[7:0]), .in1(mem_in[7:0]), .out(multiplexer_3_out), .sel(mem_addr[0]));
  Multiplexer #(.width(8)) multiplexer_4 (
    .in0(multiplexer_3_out), .in1(mem_in[7:0]), .out(multiplexer_4_out), .sel(mem_addr[1]));
  Multiplexer #(.width(8)) multiplexer_5 (
    .in0(mem_in[15:8]), .in1(rs2_val[7:0]), .out(multiplexer_5_out), .sel(mem_addr[0]));
  Multiplexer #(.width(8)) multiplexer_6 (
    .in0(multiplexer_5_out), .in1(mem_in[15:8]), .out(multiplexer_6_out), .sel(mem_addr[1]));
  Multiplexer #(.width(8)) multiplexer_7 (
    .in0(mem_in[23:16]), .in1(multiplexer_8_out), .out(multiplexer_7_out), .sel(mem_addr[1]));
  Multiplexer #(.width(8)) multiplexer_8 (
    .in0(rs2_val[7:0]), .in1(mem_in[23:16]), .out(multiplexer_8_out), .sel(mem_addr[0]));
  Multiplexer #(.width(8)) multiplexer_9 (
    .in0(mem_in[31:24]), .in1(multiplexer_10_out), .out(multiplexer_9_out), .sel(mem_addr[1]));
  Multiplexer #(.width(8)) multiplexer_10 (
    .in0(mem_in[31:24]), .in1(rs2_val[7:0]), .out(multiplexer_10_out), .sel(mem_addr[0]));
  Multiplexer #(.select(2)) multiplexer_11 (
    .in0(1'b0), .in1(mem_addr[0]), .in2(or_1_out), .in3(1'b1), .out(multiplexer_11_out), .sel(funct3[1:0]));
  Multiplexer #(.select(2), .width(32)) multiplexer_12 (
    .in0({multiplexer_9_out, multiplexer_7_out, multiplexer_6_out, multiplexer_4_out}),
    .in1({multiplexer_2_out, multiplexer_1_out}), .in2(rs2_val),
    .in3({multiplexer_9_out, multiplexer_7_out, multiplexer_6_out, multiplexer_4_out}), .out(mem_out),
    .sel(funct3[1:0]));
  Multiplexer multiplexer_13 (.in0(multiplexer_11_out), .in1(1'b1), .out(illegal_out), .sel(funct3[2]));

  // Notes on the sheet:
  //   Subword store processing
  //   Extracts a unit of data from a register value and inserts it into a memory word.
endmodule

module register_file (
  input  [4:0] rs1,
  input  [4:0] rs2,
  input  [4:0] rd,
  input  [31:0] rd_in,
  input  rd_w,
  input  clk,
  input  rst,
  output [31:0] rs1_out,
  output [31:0] rs2_out
);

  wire demultiplexer_1_out0, demultiplexer_1_out1, demultiplexer_1_out2, demultiplexer_1_out3,
       demultiplexer_2_out1, demultiplexer_2_out2, demultiplexer_2_out3, demultiplexer_2_out4,
       demultiplexer_2_out5, demultiplexer_2_out6, demultiplexer_2_out7, demultiplexer_3_out0,
       demultiplexer_3_out1, demultiplexer_3_out2, demultiplexer_3_out3, demultiplexer_3_out4,
       demultiplexer_3_out5, demultiplexer_3_out6, demultiplexer_3_out7, demultiplexer_4_out0,
       demultiplexer_4_out1, demultiplexer_4_out2, demultiplexer_4_out3, demultiplexer_4_out4,
       demultiplexer_4_out5, demultiplexer_4_out6, demultiplexer_4_out7, demultiplexer_5_out0,
       demultiplexer_5_out1, demultiplexer_5_out2, demultiplexer_5_out3, demultiplexer_5_out4,
       demultiplexer_5_out5, demultiplexer_5_out6, demultiplexer_5_out7;
  wire [31:0] multiplexer_1_out, multiplexer_2_out, multiplexer_3_out, multiplexer_4_out, multiplexer_5_out,
       multiplexer_6_out, multiplexer_7_out, multiplexer_8_out, register_1_q, register_2_q, register_3_q,
       register_4_q, register_5_q, register_6_q, register_7_q, register_8_q, register_9_q, register_10_q,
       register_11_q, register_12_q, register_13_q, register_14_q, register_15_q, register_16_q,
       register_17_q, register_18_q, register_19_q, register_20_q, register_21_q, register_22_q,
       register_23_q, register_24_q, register_25_q, register_26_q, register_27_q, register_28_q,
       register_29_q, register_30_q, register_31_q;

  Demultiplexer #(.select(2)) demultiplexer_1 (
    .out0(demultiplexer_1_out0), .out1(demultiplexer_1_out1), .out2(demultiplexer_1_out2),
    .out3(demultiplexer_1_out3), .in(rd_w), .sel(rd[4:3]));
  Demultiplexer #(.select(3)) demultiplexer_2 (
    .out1(demultiplexer_2_out1), .out2(demultiplexer_2_out2), .out3(demultiplexer_2_out3),
    .out4(demultiplexer_2_out4), .out5(demultiplexer_2_out5), .out6(demultiplexer_2_out6),
    .out7(demultiplexer_2_out7), .in(demultiplexer_1_out0), .sel(rd[2:0]));  // open: out0
  Register #(.width(32)) register_1 (.D(rd_in), .en(demultiplexer_2_out1), .clk(clk), .Q(register_1_q), .clr(rst));
  Register #(.width(32)) register_2 (.D(rd_in), .en(demultiplexer_2_out2), .clk(clk), .Q(register_2_q));  // open: clr
  Register #(.width(32)) register_3 (.D(rd_in), .en(demultiplexer_2_out3), .clk(clk), .Q(register_3_q), .clr(rst));
  Register #(.width(32)) register_4 (.D(rd_in), .en(demultiplexer_2_out4), .clk(clk), .Q(register_4_q), .clr(rst));
  Register #(.width(32)) register_5 (.D(rd_in), .en(demultiplexer_2_out5), .clk(clk), .Q(register_5_q), .clr(rst));
  Register #(.width(32)) register_6 (.D(rd_in), .en(demultiplexer_2_out6), .clk(clk), .Q(register_6_q), .clr(rst));
  Register #(.width(32)) register_7 (.D(rd_in), .en(demultiplexer_2_out7), .clk(clk), .Q(register_7_q), .clr(rst));
  Multiplexer #(.select(3), .width(32)) multiplexer_1 (
    .in0({32{1'b0}}), .in1(register_1_q), .in2(register_2_q), .in3(register_3_q), .in4(register_4_q),
    .in5(register_5_q), .in6(register_6_q), .in7(register_7_q), .out(multiplexer_1_out), .sel(rs1[2:0]));
  Multiplexer #(.select(3), .width(32)) multiplexer_2 (
    .in0({32{1'b0}}), .in1(register_1_q), .in2(register_2_q), .in3(register_3_q), .in4(register_4_q),
    .in5(register_5_q), .in6(register_6_q), .in7(register_7_q), .out(multiplexer_2_out), .sel(rs2[2:0]));
  Demultiplexer #(.select(3)) demultiplexer_3 (
    .out0(demultiplexer_3_out0), .out1(demultiplexer_3_out1), .out2(demultiplexer_3_out2),
    .out3(demultiplexer_3_out3), .out4(demultiplexer_3_out4), .out5(demultiplexer_3_out5),
    .out6(demultiplexer_3_out6), .out7(demultiplexer_3_out7), .in(demultiplexer_1_out1), .sel(rd[2:0]));
  Register #(.width(32)) register_8 (.D(rd_in), .en(demultiplexer_3_out0), .clk(clk), .Q(register_8_q), .clr(rst));
  Register #(.width(32)) register_9 (.D(rd_in), .en(demultiplexer_3_out1), .clk(clk), .Q(register_9_q), .clr(rst));
  Register #(.width(32)) register_10 (.D(rd_in), .en(demultiplexer_3_out2), .clk(clk), .Q(register_10_q));  // open: clr
  Register #(.width(32)) register_11 (.D(rd_in), .en(demultiplexer_3_out3), .clk(clk), .Q(register_11_q), .clr(rst));
  Register #(.width(32)) register_12 (.D(rd_in), .en(demultiplexer_3_out4), .clk(clk), .Q(register_12_q), .clr(rst));
  Register #(.width(32)) register_13 (.D(rd_in), .en(demultiplexer_3_out5), .clk(clk), .Q(register_13_q), .clr(rst));
  Register #(.width(32)) register_14 (.D(rd_in), .en(demultiplexer_3_out6), .clk(clk), .Q(register_14_q), .clr(rst));
  Register #(.width(32)) register_15 (.D(rd_in), .en(demultiplexer_3_out7), .clk(clk), .Q(register_15_q), .clr(rst));
  Multiplexer #(.select(3), .width(32)) multiplexer_3 (
    .in0(register_8_q), .in1(register_9_q), .in2(register_10_q), .in3(register_11_q), .in4(register_12_q),
    .in5(register_13_q), .in6(register_14_q), .in7(register_15_q), .out(multiplexer_3_out), .sel(rs1[2:0]));
  Multiplexer #(.select(3), .width(32)) multiplexer_4 (
    .in0(register_8_q), .in1(register_9_q), .in2(register_10_q), .in3(register_11_q), .in4(register_12_q),
    .in5(register_13_q), .in6(register_14_q), .in7(register_15_q), .out(multiplexer_4_out), .sel(rs2[2:0]));
  Demultiplexer #(.select(3)) demultiplexer_4 (
    .out0(demultiplexer_4_out0), .out1(demultiplexer_4_out1), .out2(demultiplexer_4_out2),
    .out3(demultiplexer_4_out3), .out4(demultiplexer_4_out4), .out5(demultiplexer_4_out5),
    .out6(demultiplexer_4_out6), .out7(demultiplexer_4_out7), .in(demultiplexer_1_out2), .sel(rd[2:0]));
  Register #(.width(32)) register_16 (.D(rd_in), .en(demultiplexer_4_out0), .clk(clk), .Q(register_16_q), .clr(rst));
  Register #(.width(32)) register_17 (.D(rd_in), .en(demultiplexer_4_out1), .clk(clk), .Q(register_17_q), .clr(rst));
  Register #(.width(32)) register_18 (.D(rd_in), .en(demultiplexer_4_out2), .clk(clk), .Q(register_18_q));  // open: clr
  Register #(.width(32)) register_19 (.D(rd_in), .en(demultiplexer_4_out3), .clk(clk), .Q(register_19_q), .clr(rst));
  Register #(.width(32)) register_20 (.D(rd_in), .en(demultiplexer_4_out4), .clk(clk), .Q(register_20_q), .clr(rst));
  Register #(.width(32)) register_21 (.D(rd_in), .en(demultiplexer_4_out5), .clk(clk), .Q(register_21_q), .clr(rst));
  Register #(.width(32)) register_22 (.D(rd_in), .en(demultiplexer_4_out6), .clk(clk), .Q(register_22_q), .clr(rst));
  Register #(.width(32)) register_23 (.D(rd_in), .en(demultiplexer_4_out7), .clk(clk), .Q(register_23_q), .clr(rst));
  Multiplexer #(.select(3), .width(32)) multiplexer_5 (
    .in0(register_16_q), .in1(register_17_q), .in2(register_18_q), .in3(register_19_q), .in4(register_20_q),
    .in5(register_21_q), .in6(register_22_q), .in7(register_23_q), .out(multiplexer_5_out), .sel(rs1[2:0]));
  Multiplexer #(.select(3), .width(32)) multiplexer_6 (
    .in0(register_16_q), .in1(register_17_q), .in2(register_18_q), .in3(register_19_q), .in4(register_20_q),
    .in5(register_21_q), .in6(register_22_q), .in7(register_23_q), .out(multiplexer_6_out), .sel(rs2[2:0]));
  Demultiplexer #(.select(3)) demultiplexer_5 (
    .out0(demultiplexer_5_out0), .out1(demultiplexer_5_out1), .out2(demultiplexer_5_out2),
    .out3(demultiplexer_5_out3), .out4(demultiplexer_5_out4), .out5(demultiplexer_5_out5),
    .out6(demultiplexer_5_out6), .out7(demultiplexer_5_out7), .in(demultiplexer_1_out3), .sel(rd[2:0]));
  Register #(.width(32)) register_24 (.D(rd_in), .en(demultiplexer_5_out0), .clk(clk), .Q(register_24_q), .clr(rst));
  Register #(.width(32)) register_25 (.D(rd_in), .en(demultiplexer_5_out1), .clk(clk), .Q(register_25_q), .clr(rst));
  Register #(.width(32)) register_26 (.D(rd_in), .en(demultiplexer_5_out2), .clk(clk), .Q(register_26_q));  // open: clr
  Register #(.width(32)) register_27 (.D(rd_in), .en(demultiplexer_5_out3), .clk(clk), .Q(register_27_q), .clr(rst));
  Register #(.width(32)) register_28 (.D(rd_in), .en(demultiplexer_5_out4), .clk(clk), .Q(register_28_q), .clr(rst));
  Register #(.width(32)) register_29 (.D(rd_in), .en(demultiplexer_5_out5), .clk(clk), .Q(register_29_q), .clr(rst));
  Register #(.width(32)) register_30 (.D(rd_in), .en(demultiplexer_5_out6), .clk(clk), .Q(register_30_q), .clr(rst));
  Register #(.width(32)) register_31 (.D(rd_in), .en(demultiplexer_5_out7), .clk(clk), .Q(register_31_q), .clr(rst));
  Multiplexer #(.select(3), .width(32)) multiplexer_7 (
    .in0(register_24_q), .in1(register_25_q), .in2(register_26_q), .in3(register_27_q), .in4(register_28_q),
    .in5(register_29_q), .in6(register_30_q), .in7(register_31_q), .out(multiplexer_7_out), .sel(rs1[2:0]));
  Multiplexer #(.select(3), .width(32)) multiplexer_8 (
    .in0(register_24_q), .in1(register_25_q), .in2(register_26_q), .in3(register_27_q), .in4(register_28_q),
    .in5(register_29_q), .in6(register_30_q), .in7(register_31_q), .out(multiplexer_8_out), .sel(rs2[2:0]));
  Multiplexer #(.select(2), .width(32)) multiplexer_9 (
    .in0(multiplexer_1_out), .in1(multiplexer_3_out), .in2(multiplexer_5_out), .in3(multiplexer_7_out),
    .out(rs1_out), .sel(rs1[4:3]));
  Multiplexer #(.select(2), .width(32)) multiplexer_10 (
    .in0(multiplexer_2_out), .in1(multiplexer_4_out), .in2(multiplexer_6_out), .in3(multiplexer_8_out),
    .out(rs2_out), .sel(rs2[4:3]));

  // Notes on the sheet:
  //   Register file
  //   The 32 base registers. Register x0 is hardwired to 0. Program counter is not included.
endmodule

module program_counter (
  input  [31:0] pc_in,
  input  clk,
  input  rst,
  output [31:0] pc,
  output [31:0] pc_next
);

  Register #(.width(32)) register_1 (.D(pc_in), .en(1'b1), .clk(clk), .Q(pc), .clr(rst));
  Adder #(.width(32)) adder_1 (.a(pc), .b(32'h4), .out(pc_next), .cin(1'b0));  // open: cout

  // Notes on the sheet:
  //   Program counter
  //   Provides both the address of the current instruction as well as the address of the next one.
endmodule

module control_unit (
  input  [31:0] rs1,
  input  [31:0] rs2,
  input  [31:0] pc,
  input  [31:0] pc_next,
  input  [31:0] imm_i,
  input  [31:0] imm_s,
  input  [31:0] imm_b,
  input  [31:0] imm_u,
  input  [31:0] imm_j,
  input  [3:0] inst_t,
  input  [2:0] funct3,
  input  [6:0] funct7,
  output [31:0] rd_val,
  output illegal
);

  wire and_1_out, and_2_out, and_3_out, comparator_1_eq, comparator_1_lt, comparator_2_lt,
       funct7_validation_1_illegal, multiplexer_4_out, not_1_out, not_2_out, not_3_out;
  wire [2:0] multiplexer_3_out;
  wire [6:0] funct7_validation_1_funct7_out;
  wire [31:0] arithmetic_logic_unit_1_result, multiplexer_1_out, multiplexer_2_out, multiplexer_5_out;

  Multiplexer #(.select(4), .width(32)) multiplexer_1 (
    .in0({32{1'b0}}), .in1(rs1), .in2(rs1), .in3(pc), .in4({32{1'b0}}), .in5(rs1), .in6(rs1), .in7(pc),
    .in8(rs1), .in9(pc), .in10({32{1'b0}}), .in11({32{1'b0}}), .in12({32{1'b0}}), .in13({32{1'b0}}),
    .in14({32{1'b0}}), .in15({32{1'b0}}), .out(multiplexer_1_out), .sel(inst_t));
  Multiplexer #(.select(4), .width(32)) multiplexer_2 (
    .in0({32{1'b0}}), .in1(rs2), .in2(imm_i), .in3(imm_u), .in4(imm_u), .in5(imm_i), .in6(imm_s),
    .in7(imm_b), .in8(imm_i), .in9(imm_j), .in10({32{1'b0}}), .in11({32{1'b0}}), .in12({32{1'b0}}),
    .in13({32{1'b0}}), .in14({32{1'b0}}), .in15({32{1'b0}}), .out(multiplexer_2_out), .sel(inst_t));
  Multiplexer #(.select(4), .width(3)) multiplexer_3 (
    .in0(3'b000), .in1(funct3), .in2(funct3), .in3(3'b000), .in4(3'b000), .in5(3'b000), .in6(3'b000),
    .in7(3'b000), .in8(3'b000), .in9(3'b000), .in10(3'b000), .in11(3'b000), .in12(3'b000), .in13(3'b000),
    .in14(3'b000), .in15(3'b000), .out(multiplexer_3_out), .sel(inst_t));
  and and_1 (and_1_out, funct3[1], ~funct3[2], inst_t[0], inst_t[1], inst_t[2], ~inst_t[3]);  // AND_Gate
  Comparator #(.width(32)) comparator_1 (.a(rs1), .b(rs2), .eq(comparator_1_eq), .lt(comparator_1_lt));  // open: gt
  Comparator #(.mode("unsigned"), .width(32)) comparator_2 (.a(rs1), .b(rs2), .lt(comparator_2_lt));  // open: gt, eq
  not not_1 (not_1_out, comparator_1_eq);
  funct7_validation funct7_validation_1 (
    .funct3(funct3), .inst_t(inst_t), .funct7_in(funct7), .funct7_out(funct7_validation_1_funct7_out),
    .illegal(funct7_validation_1_illegal));
  not not_2 (not_2_out, comparator_1_lt);
  not not_3 (not_3_out, comparator_2_lt);
  Multiplexer #(.select(3)) multiplexer_4 (
    .in0(comparator_1_eq), .in1(not_1_out), .in2(1'b0), .in3(1'b0), .in4(comparator_1_lt), .in5(not_2_out),
    .in6(comparator_2_lt), .in7(not_3_out), .out(multiplexer_4_out), .sel(funct3));
  arithmetic_logic_unit arithmetic_logic_unit_1 (
    .operand_1(multiplexer_1_out), .operand_2(multiplexer_2_out), .funct7(funct7_validation_1_funct7_out),
    .funct3(multiplexer_3_out), .result(arithmetic_logic_unit_1_result));
  Multiplexer #(.width(32)) multiplexer_5 (
    .in0(arithmetic_logic_unit_1_result), .in1(pc_next), .out(multiplexer_5_out), .sel(and_2_out));
  and and_2 (and_2_out, ~multiplexer_4_out, and_3_out);  // AND_Gate
  or or_1 (illegal, funct7_validation_1_illegal, and_1_out);
  and and_3 (and_3_out, ~inst_t[3], inst_t[2], inst_t[1], inst_t[0]);  // AND_Gate
  Multiplexer #(.width(32)) multiplexer_6 (.in0(multiplexer_5_out), .in1({32{1'b0}}), .out(rd_val), .sel(illegal));

  // Notes on the sheet:
  //   Control unit
  //   Validates inputs and passes the appropriate values to the ALU.
endmodule

module funct7_validation (
  input  [2:0] funct3,
  input  [3:0] inst_t,
  input  [6:0] funct7_in,
  output [6:0] funct7_out,
  output illegal
);

  wire or_1_out, pla_1_out;

  PLA #(.in_width(7), .out_width(1), .\table ("0000xxx 0 # X\n0001xxx 1 # OP\n0010000 0 # IMM\n0010001 1 # SHIFT\n001001x 0 # IMM\n0010100 0 # IMM\n0010101 1 # SHIFT\n001011x 0 # IMM\n0011xxx 0 # X\n01xxxxx 0 # X\n1xxxxxx 0 # X")) pla_1 (
    .in({inst_t, funct3}), .out(pla_1_out));
  Multiplexer #(.width(7)) multiplexer_1 (.in0({7{1'b0}}), .in1(funct7_in), .out(funct7_out), .sel(pla_1_out));
  or or_1 (or_1_out, funct7_in[0], funct7_in[1], funct7_in[2], funct7_in[3], funct7_in[4], funct7_in[6]);
  Multiplexer multiplexer_2 (.in0(1'b0), .in1(or_1_out), .out(illegal), .sel(pla_1_out));

  // Notes on the sheet:
  //   'funct7' validation
  //   Make sure the 'funct7' value is valid.
endmodule

module arithmetic_logic_unit (
  input  [31:0] operand_1,
  input  [31:0] operand_2,
  input  [6:0] funct7,
  input  [2:0] funct3,
  output [31:0] result
);

  wire [0:0] comparator_1_lt, comparator_2_lt;
  wire [31:0] adder_1_out, and_1_out, multiplexer_1_out, multiplexer_2_out, or_1_out, shifter_1_out,
       shifter_2_out, shifter_3_out, subtractor_1_out, xor_1_out;

  Adder #(.width(32)) adder_1 (.a(operand_1), .b(operand_2), .out(adder_1_out));  // open: cin, cout
  Subtractor #(.width(32)) subtractor_1 (.a(operand_1), .b(operand_2), .out(subtractor_1_out));  // open: bin, bout
  Comparator #(.width(32)) comparator_1 (.a(operand_1), .b(operand_2), .lt(comparator_1_lt[0]));  // open: gt, eq
  Comparator #(.mode("unsigned"), .width(32)) comparator_2 (
    .a(operand_1), .b(operand_2), .lt(comparator_2_lt[0]));  // open: gt, eq
  Shifter #(.width(32)) shifter_1 (.in(operand_1), .\dist (operand_2[4:0]), .out(shifter_1_out));
  Shifter #(.shift("lr"), .width(32)) shifter_2 (.in(operand_1), .\dist (operand_2[4:0]), .out(shifter_2_out));
  Shifter #(.shift("ar"), .width(32)) shifter_3 (.in(operand_1), .\dist (operand_2[4:0]), .out(shifter_3_out));
  assign xor_1_out = operand_1 ^ operand_2;  // XOR_Gate xor_1, 32 bits wide
  assign or_1_out = operand_1 | operand_2;  // OR_Gate or_1, 32 bits wide
  assign and_1_out = operand_1 & operand_2;  // AND_Gate and_1, 32 bits wide
  Multiplexer #(.width(32)) multiplexer_1 (
    .in0(adder_1_out), .in1(subtractor_1_out), .out(multiplexer_1_out), .sel(funct7[5]));
  Multiplexer #(.width(32)) multiplexer_2 (
    .in0(shifter_2_out), .in1(shifter_3_out), .out(multiplexer_2_out), .sel(funct7[5]));
  Multiplexer #(.select(3), .width(32)) multiplexer_3 (
    .in0(multiplexer_1_out), .in1(shifter_1_out), .in2({{31{1'b0}}, comparator_1_lt[0]}),
    .in3({{31{1'b0}}, comparator_2_lt[0]}), .in4(xor_1_out), .in5(multiplexer_2_out), .in6(or_1_out),
    .in7(and_1_out), .out(result), .sel(funct3));

  // Notes on the sheet:
  //   Arithmetic logic unit
  //   Calculates values for arithmetic, logic, and bit shift operations. Assumes 'funct3' and 'funct7' are valid.
endmodule

module example_hello_world (
  input  rst,
  output [31:0] out_2,
  output [31:0] out_3,
  output [31:0] out_4
);

  wire alpha_core_1_mem_write, clk_out, decoder_1_out0, decoder_1_out1, decoder_1_out2, decoder_1_out3;
  wire [1:0] bcd_to_7_segment_decoder_1_p1;
  wire [31:0] ram_1_dout, rom_1_data;

  Clock clk (.out(clk_out));
  _7_Segment_Display u_7_segment_display_1 ();  // open: g, f, a, b, e, d, c, dp
  // BCD_to_7_Segment_decoder bcd_to_7_segment_decoder_1: pin names not known; wires that end beside it: {2'b00, bcd_to_7_segment_decoder_1_p1}
  alpha_core alpha_core_1 (
    .mem_in(out_2), .clk(clk_out), .rst(rst), .mem_addr(out_3), .mem_out(out_4),
    .mem_write(alpha_core_1_mem_write), .state(bcd_to_7_segment_decoder_1_p1));
  Decoder #(.select(2)) decoder_1 (
    .out0(decoder_1_out0), .out1(decoder_1_out1), .out2(decoder_1_out2), .out3(decoder_1_out3),
    .sel(out_3[17:16]), .en(alpha_core_1_mem_write));
  Multiplexer #(.select(2), .width(32)) multiplexer_1 (
    .in0(rom_1_data), .in1(ram_1_dout), .in2({32{1'b0}}), .in3({32{1'b0}}), .out(out_2), .sel(out_3[17:16]));
  ROM #(.addrWidth(14), .dataWidth(32)) rom_1 (.addr(out_3[15:2]), .data(rom_1_data));
  RAM #(.addrWidth(14), .dataWidth(32), .enables("line")) ram_1 (
    .addr(out_3[15:2]), .we(decoder_1_out1), .clk(clk_out), .din(out_4), .dout(ram_1_dout));
  TTY tty_1 (.data(out_4[6:0]), .clk(clk_out), .we(decoder_1_out2), .clr(rst));

  // Notes on the sheet:
  //   contents of rom_1 (hex, n*v repeats v):
  //   517 42050513 3b4000ef 517 70150513 3a8000ef 517 43750513 39c000ef 517 43d50513 390000ef 12342b7
  //   56728293 89abd337 def30313 628533 394000ef 517 6c350513 36c000ef 517 42f50513 360000ef 12342b7
  //   56728293 89abd337 def30313 40628533 364000ef 517 69350513 33c000ef 517 42150513 330000ef 12342b7
  //   56728293 89abd337 def30313 62c533 334000ef 517 66350513 30c000ef 517 41350513 300000ef 12342b7
  //   56728293 89abd337 def30313 62e533 304000ef 517 63350513 2dc000ef 517 40550513 2d0000ef 12342b7
  //   56728293 89abd337 def30313 62f533 2d4000ef 517 60350513 2ac000ef 517 3f750513 2a0000ef 12342b7
  //   56728293 89abd337 def30313 629533 2a4000ef 517 5d350513 27c000ef 517 3e950513 270000ef 12342b7
  //   56728293 89abd337 def30313 62d533 274000ef 517 5a350513 24c000ef 517 3db50513 240000ef 12342b7
  //   56728293 89abd337 def30313 4062d533 244000ef 517 57350513 21c000ef 517 3cd50513 210000ef 12342b7
  //   56728293 89abd337 def30313 62a533 214000ef 517 54350513 1ec000ef 517 3bf50513 1e0000ef 12342b7
  //   56728293 89abd337 def30313 62b533 1e4000ef 517 51350513 1bc000ef 517 50950513 1b0000ef 517 3a550513
  //   1a4000ef 517 3af50513 198000ef 12342b7 56728293 12328513 1a4000ef 517 4d350513 17c000ef 517 3a650513
  //   170000ef 12342b7 56728293 edd28513 17c000ef 517 4ab50513 154000ef 517 39d50513 148000ef 12342b7
  //   56728293 1232c513 154000ef 517 48350513 12c000ef 517 39450513 120000ef 12342b7 56728293 1232e513
  //   12c000ef 517 45b50513 104000ef 517 38b50513 f8000ef 12342b7 56728293 1232f513 104000ef 517 43350513
  //   dc000ef 517 38250513 d0000ef 89abd2b7 def28293 1229513 dc000ef 517 40b50513 b4000ef 517 37850513
  //   a8000ef 89abd2b7 def28293 122d513 b4000ef 517 3e350513 8c000ef 517 36e50513 80000ef 89abd2b7
  //   def28293 4122d513 8c000ef 517 3bb50513 64000ef 517 36450513 58000ef 89abd2b7 def28293 122a513
  //   64000ef 517 39350513 3c000ef 517 35a50513 30000ef 89abd2b7 def28293 122b513 3c000ef 517 36b50513
  //   14000ef 517 36150513 8000ef 640006f 20337 54283 28863 530023 150513 ff1ff06f 8067 20337 3000293
  //   530023 7800293 530023 800393 3a00e13 1c55293 451513 556533 fff38393 3028293 1c2c463 2728293 530023
  //   fe7040e3 8067 0 32335652 6f632049 203a6572 706c6127 a276168 74736554 20676e69 206c6c61 74736e69
  //   74637572 736e6f69 4f000a2e 6e692050 75727473 6f697463 a3a736e 20202000 64646120 78302020 33323130
  //   37363534 7830202c 62613938 66656463 2000203a 73202020 20206275 31307830 35343332 202c3736 39387830
  //   64636261 203a6665 20202000 726f7820 78302020 33323130 37363534 7830202c 62613938 66656463 2000203a
  //   6f202020 20202072 31307830 35343332 202c3736 39387830 64636261 203a6665 20202000 646e6120 78302020
  //   33323130 37363534 7830202c 62613938 66656463 2000203a 73202020 20206c6c 31307830 35343332 202c3736
  //   39387830 64636261 203a6665 20202000 6c727320 78302020 33323130 37363534 7830202c 62613938 66656463
  //   2000203a 73202020 20206172 31307830 35343332 202c3736 39387830 64636261 203a6665 20202000 746c7320
  //   78302020 33323130 37363534 7830202c 62613938 66656463 2000203a 73202020 2075746c 31307830 35343332
  //   202c3736 39387830 64636261 203a6665 5f504f00 204d4d49 74736e69 74637572 736e6f69 20000a3a 61202020
  //   20696464 30783020 34333231 2c373635 78302020 3a333231 20200020 64612020 20206964 31307830 35343332
  //   202c3736 3178302d 203a3332 20202000 726f7820 30202069 32313078 36353433 20202c37 32317830 203a33
  //   20202020 2069726f 78302020 33323130 37363534 3020202c 33323178 2000203a 61202020 2069646e 30783020
  //   34333231 2c373635 78302020 3a333231 20200020 6c732020 2020696c 39387830 64636261 202c6665 31783020
  //   203a32 20202020 696c7273 78302020 62613938 66656463 3020202c 3a323178 20200020 72732020 20206961
  //   39387830 64636261 202c6665 31783020 203a32 20202020 69746c73 78302020 62613938 66656463 3020202c
  //   3a323178 20200020 6c732020 20756974 39387830 64636261 202c6665 31783020 203a32 6c6c6548 57202c6f
  //   646c726f a000a21 2d2d2d00 5*2d2d2d2d a2d2d
endmodule

module example_test_all_instructions (
  input  rst,
  output [31:0] out_2,
  output [31:0] out_3,
  output [31:0] out_4
);

  wire alpha_core_1_mem_write, clk_out, decoder_1_out0, decoder_1_out1, decoder_1_out2, decoder_1_out3;
  wire [1:0] bcd_to_7_segment_decoder_1_p1;
  wire [31:0] ram_1_dout, rom_1_data;

  Clock clk (.out(clk_out));
  _7_Segment_Display u_7_segment_display_1 ();  // open: g, f, a, b, e, d, c, dp
  // BCD_to_7_Segment_decoder bcd_to_7_segment_decoder_1: pin names not known; wires that end beside it: {2'b00, bcd_to_7_segment_decoder_1_p1}
  alpha_core alpha_core_1 (
    .mem_in(out_2), .clk(clk_out), .rst(rst), .mem_addr(out_3), .mem_out(out_4),
    .mem_write(alpha_core_1_mem_write), .state(bcd_to_7_segment_decoder_1_p1));
  Decoder #(.select(2)) decoder_1 (
    .out0(decoder_1_out0), .out1(decoder_1_out1), .out2(decoder_1_out2), .out3(decoder_1_out3),
    .sel(out_3[17:16]), .en(alpha_core_1_mem_write));
  Multiplexer #(.select(2), .width(32)) multiplexer_1 (
    .in0(rom_1_data), .in1(ram_1_dout), .in2({32{1'b0}}), .in3({32{1'b0}}), .out(out_2), .sel(out_3[17:16]));
  ROM #(.addrWidth(14), .dataWidth(32)) rom_1 (.addr(out_3[15:2]), .data(rom_1_data));
  RAM #(.addrWidth(14), .dataWidth(32), .enables("line")) ram_1 (
    .addr(out_3[15:2]), .we(decoder_1_out1), .clk(clk_out), .din(out_4), .dout(ram_1_dout));
  TTY #(.cols(80), .rows(16)) tty_1 (.data(out_4[6:0]), .clk(clk_out), .we(decoder_1_out2), .clr(rst));

  // Notes on the sheet:
  //   contents of rom_1 (hex, n*v repeats v):
  //   1517 ae050513 275000ef 1517 24150513 269000ef 1517 af750513 25d000ef 1517 afd50513 251000ef 12342b7
  //   56728293 89abd337 def30313 628533 255000ef 1517 20050513 22d000ef 1517 aef50513 221000ef 12342b7
  //   56728293 89abd337 def30313 40628533 225000ef 1517 1d050513 1fd000ef 1517 ae150513 1f1000ef 12342b7
  //   56728293 89abd337 def30313 62c533 1f5000ef 1517 1a050513 1cd000ef 1517 ad350513 1c1000ef 12342b7
  //   56728293 89abd337 def30313 62e533 1c5000ef 1517 17050513 19d000ef 1517 ac550513 191000ef 12342b7
  //   56728293 89abd337 def30313 62f533 195000ef 1517 14050513 16d000ef 1517 ab750513 161000ef 12342b7
  //   56728293 89abd337 def30313 629533 165000ef 1517 11050513 13d000ef 1517 aa950513 131000ef 12342b7
  //   56728293 89abd337 def30313 62d533 135000ef 1517 e050513 10d000ef 1517 a9b50513 101000ef 12342b7
  //   56728293 89abd337 def30313 4062d533 105000ef 1517 b050513 dd000ef 1517 a8d50513 d1000ef 12342b7
  //   56728293 89abd337 def30313 62a533 d5000ef 1517 8050513 ad000ef 1517 a7f50513 a1000ef 12342b7
  //   56728293 89abd337 def30313 62b533 a5000ef 1517 5050513 7d000ef 1517 4950513 71000ef 1517 a6550513
  //   65000ef 1517 a6f50513 59000ef 12342b7 56728293 12328513 65000ef 1517 1050513 3d000ef 1517 a6650513
  //   31000ef 12342b7 56728293 edd28513 3d000ef 1517 fe850513 15000ef 1517 a5d50513 9000ef 12342b7
  //   56728293 1232c513 15000ef 1517 fc050513 7ec000ef 1517 a5450513 7e0000ef 12342b7 56728293 1232e513
  //   7ec000ef 1517 f9850513 7c4000ef 1517 a4b50513 7b8000ef 12342b7 56728293 1232f513 7c4000ef 1517
  //   f7050513 79c000ef 1517 a4250513 790000ef 89abd2b7 def28293 1229513 79c000ef 1517 f4850513 774000ef
  //   1517 a3950513 768000ef 89abd2b7 def28293 122d513 774000ef 1517 f2050513 74c000ef 1517 a3050513
  //   740000ef 89abd2b7 def28293 4122d513 74c000ef 1517 ef850513 724000ef 1517 a2750513 718000ef 89abd2b7
  //   def28293 122a513 724000ef 1517 ed050513 6fc000ef 1517 a1e50513 6f0000ef 89abd2b7 def28293 122b513
  //   6fc000ef 1517 ea850513 6d4000ef 1517 ea150513 6c8000ef 1517 a0950513 6bc000ef 1517 a1350513 6b0000ef
  //   12300293 45600313 628863 1517 e9150513 c0006f 1517 e8050513 68c000ef 1517 9fb50513 680000ef 12300293
  //   12300313 628863 1517 e6150513 c0006f 1517 e5050513 65c000ef 1517 9e350513 650000ef 12300293 45600313
  //   629863 1517 e3150513 c0006f 1517 e2050513 62c000ef 1517 9cb50513 620000ef 12300293 12300313 629863
  //   1517 e0150513 c0006f 1517 df050513 5fc000ef 1517 9b350513 5f0000ef 12300293 45600313 62c863 1517
  //   dd150513 c0006f 1517 dc050513 5cc000ef 1517 99b50513 5c0000ef 12300293 12300313 62c863 1517 da150513
  //   c0006f 1517 d9050513 59c000ef 1517 98350513 590000ef 45600293 12300313 62c863 1517 d7150513 c0006f
  //   1517 d6050513 56c000ef 1517 96b50513 560000ef 12300293 45600313 62d863 1517 d4150513 c0006f 1517
  //   d3050513 53c000ef 1517 95350513 530000ef 12300293 12300313 62d863 1517 d1150513 c0006f 1517 d0050513
  //   50c000ef 1517 93b50513 500000ef 45600293 12300313 62d863 1517 ce150513 c0006f 1517 cd050513 4dc000ef
  //   1517 92350513 4d0000ef 123002b7 f4560337 62e863 1517 cb150513 c0006f 1517 ca050513 4ac000ef 1517
  //   91550513 4a0000ef 123002b7 12300337 62e863 1517 c8150513 c0006f 1517 c7050513 47c000ef 1517 90750513
  //   470000ef f45602b7 12300337 62e863 1517 c5150513 c0006f 1517 c4050513 44c000ef 1517 8f950513 440000ef
  //   123002b7 f4560337 62f863 1517 c2150513 c0006f 1517 c1050513 41c000ef 1517 8eb50513 410000ef 123002b7
  //   12300337 62f863 1517 bf150513 c0006f 1517 be050513 3ec000ef 1517 8dd50513 3e0000ef f45602b7 12300337
  //   62f863 1517 bc150513 c0006f 1517 bb050513 3bc000ef 1517 b8950513 3b0000ef 1517 8c350513 3a4000ef
  //   1517 8dc50513 398000ef 1517 8f450513 297 38c28293 280e7 1517 90550513 378000ef 12345537 38c000ef
  //   1517 b3850513 364000ef 1517 8f950513 358000ef 12345517 36c000ef 1517 b1850513 344000ef 1517 b1150513
  //   338000ef 1517 8e150513 32c000ef 105b7 5a023 5a223 5a423 1517 8e350513 310000ef 1517 8f450513
  //   304000ef 5a503 318000ef 1517 ac650513 2f0000ef 45a503 304000ef 1517 ab250513 2dc000ef 85a503
  //   2f0000ef 1517 a9c50513 2c8000ef 12345537 67850513 a5a023 1517 8af50513 2b0000ef abcdf537 fff50513
  //   a5a223 1517 8bf50513 298000ef 76543537 21050513 a5a423 1517 8cf50513 280000ef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
endmodule
